# Fritzing sketch disenio_esquema (saved by Fritzing 0.9.2b)
breadboards: 1

parts:
  Raspberry_Pi1 = Raspberry Pi 2
  Servomotor = Basic Servo
  Modulo_wifi = USB_MICROB_PLUG [package=micro-b-ra-th]  # not connected
  Voice_Tracker_II = DB9 Connector [package=db9]  # not connected
  Camera = TRANSCHIPTC5747 [package=camera_sfv24r-2st_2]  # not connected

nets:
  N1: Raspberry_Pi1.GPIO11, Servomotor.pulse
  GND: Raspberry_Pi1.GND, Servomotor.gnd
  5V: Raspberry_Pi1.5V, Servomotor.vcc

notes:
  Audio
  Datos
